// Logisim project 2 bit alu.circ as structural Verilog
module _1_bit_alu (
  input  B,
  input  A,
  input  Carry_In,
  input  [1:0] Operation,
  input  in_5,
  output Result,
  output Carry_out
);

  wire adder_1_out, and_1_out, multiplexer_1_out, not_1_out, or_1_out;

  not not_1 (not_1_out, B);
  Multiplexer multiplexer_1 (.in0(not_1_out), .in1(B), .out(multiplexer_1_out), .sel(in_5));  // open: en
  and and_1 (and_1_out, A, multiplexer_1_out);
  or or_1 (or_1_out, A, multiplexer_1_out);
  Adder #(.width(1)) adder_1 (.a(A), .b(multiplexer_1_out), .out(adder_1_out), .cin(Carry_In), .cout(Carry_out));
  Multiplexer #(.select(2)) multiplexer_2 (
    .in0(and_1_out), .in1(or_1_out), .in2(adder_1_out), .out(Result), .sel(Operation));  // open: in3, en
  main main_1 ();
endmodule

module _2_bit_alu (
  input  in_1,
  input  [1:0] in_2,
  input  in_3,
  input  [1:0] in_4,
  output out_5
);

  wire n1_bit_alu_1_carry_out;

  _1_bit_alu u_1_bit_alu_1 (
    .B(in_4[0]), .A(in_2[0]), .Carry_In(in_1), .in_5(in_3), .Carry_out(n1_bit_alu_1_carry_out));  // open: Result, Operation
  _1_bit_alu u_1_bit_alu_2 (
    .B(in_4[1]), .A(in_2[1]), .Carry_In(n1_bit_alu_1_carry_out), .in_5(in_3), .Carry_out(out_5));  // open: Result, Operation
endmodule
